# Fritzing sketch penyiramandanpengkabutan (saved by Fritzing 0.9.5d)

parts:
  A1 = ESP32 devkit 38p expansion board
  MH-ET_LIVE_ESP32_DEVKIT1 = MH-ET LIVE ESP32 DEVKIT 38 pins  # not connected
  DHT1 = DHT11 Humitidy and Temperature Sensor (3 pins)
  PART1 = SparkFun Soil Moisture Sensor [part_number=SEN-13322]
  Part1 = SRF05 Ultrasonic Rangefinder
  U1 = 2-Channel 5v Relay Shield [package=relay-2ch5v10a]

nets:
  N1: A1.Pin_7, PART1.SIG
  N2: A1.Pin_8, Part1.Echo
  N3: A1.Pin_9, Part1.Trig
  VCC: A1.Pin_17, A1.Pin_56, A1.Pin_98, Part1.VCC, U1.VCC
  GND: A1.Pin_52, A1.Pin_53, A1.Pin_54, A1.Pin_120, A1.Pin_144, DHT1.Gnd, PART1.GND, Part1.GND, U1.GND
  N4: A1.Pin_58, A1.Pin_59, A1.Pin_100, DHT1.Plus, PART1.VCC
  N5: A1.Pin_151, A1.Pin_155, DHT1.Signal
  N6: A1.Pin_177, U1.IN2
  N7: A1.Pin_178, U1.IN1

custom parts:
  ESP32 devkit 38p expansion board: Upgraded ESP32 38P Development ESP32-DevKitC-32 ESP-WROOM-32 Expansion Board.
  MH-ET LIVE ESP32 DEVKIT 38 pins: http://mh.nodebb.com/topic/2/mh-et-live-esp32-devkit
  DHT11 Humitidy and Temperature Sensor (3 pins): DHT11 Humidity and Temperature Sensor (3 pins).
  SparkFun Soil Moisture Sensor: The SparkFun Soil Moisture Sensor is a simple breakout for measuring the moisture in soil and similar materials.
  2-Channel 5v Relay Shield: 2 Channel 5v Relay Shield w. 2x SPD-06VDC-SD-C
